# Fritzing sketch Persiana (saved by Fritzing 1.0.5)

parts:
  M1 = DOIT Esp32 DevKit v1 (30 pins long, 11 pins width) [part_number=ESP32S-PIN30]
  Part1 = Motor Driver 1A Dual TB6612FNG
  M2 = DC Motor [voltage_(max)=6V voltage_(min)=3V]
  S2 = Pushbutton [package="[THT]"]
  S3 = Pushbutton [package="[THT]"]
  S4 = Pushbutton [package="[THT]"]
  J1 = Piezo Speaker
  S5 = Pushbutton [package="[THT]"]
  VCC1 = Battery block 9V [internal_resistance=0.1Ω]
  U1 = LM2596 step down module

nets:
  3V3: M1.3V3, Part1.VCC, Part1.STBY
  GND: M1.GND, Part1.GND, S2.Pin_3, S2.Pin_4, S3.Pin_3, S3.Pin_4, S4.Pin_3, S4.Pin_4, J1.pin1, S5.Pin_3, S5.Pin_4, U1.IN-, U1.OUT-
  N1: M1.D4, J1.pin2
  N2: M1.D32, S3.Pin_1, S3.Pin_2
  N3: M1.D33, S5.Pin_1
  N4: M1.D25, Part1.AIN1
  N5: M1.D26, Part1.AIN2
  N6: M1.D27, Part1.PWMA
  N7: M1.D12, S4.Pin_1
  N8: M1.D13, S2.Pin_1, S2.Pin_2
  N9: M1.VIN, U1.OUT+
  N10: Part1.A02, M2.pin_2
  N11: Part1.A01, M2.pin_1
  N12: Part1.VM, VCC1.+

notes:
  GND
  PWMB
  BIN2
  BIN1
  STBY
  AIN1
  AIN2
  PWMA
  BO1
  BO2
  A02
  A01
  VCC
  VM
  ARRIBA
  ABAJO
  STOP
  AUTO
  12V
  D4
  D33
  5V

custom parts:
  DOIT Esp32 DevKit v1 (30 pins long, 11 pins width): The DOIT Esp32 DevKit v1 is one of the development board created by DOIT to evaluate the ESP-WROOM-32 module. It is based on the ESP32 microcontroller that boasts Wifi, Bluetooth, Ethernet and Low Power support all in a single chip. (vanepp) made breadboard work, adjusted pin numbering and labels and reduced size of schematic and cleaned up pcb. This chip is 30pins long (2 x15) and 11 pins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
  LM2596 step down module: LM2596 DC-DC step down power supply module 3 A.

// code stored in the sketch: MOTOR.ino
#include <Preferences.h>

Preferences prefs;

//==================== TB6612 ====================
#define AIN1 25
#define AIN2 26
#define PWMA 27

//==================== BOTONES ====================
#define BTN_UP     32
#define BTN_DOWN   33
#define BTN_STOP   12
#define BTN_AUTO   13

//==================== BUZZER =====================
#define BUZZER 4

//==================== PWM ========================
#define PWM_FREQ 1000
#define PWM_CH 0
#define PWM_RES 8
#define MOTOR_SPEED 180

//=================================================

bool modoProgramacion=false;
bool persianaAbierta=false;

unsigned long tiempoMax=8000;

unsigned long inicioTiempo=0;
unsigned long tiempoAcumulado=0;

String ultimoEstado="";


//=================================================

void setup() {

  Serial.begin(115200);

  prefs.begin("persiana", false);

  tiempoMax=
  prefs.getULong("tiempo",8000);

  pinMode(AIN1,OUTPUT);
  pinMode(AIN2,OUTPUT);

  pinMode(BTN_UP,INPUT_PULLUP);
  pinMode(BTN_DOWN,INPUT_PULLUP);
  pinMode(BTN_STOP,INPUT_PULLUP);
  pinMode(BTN_AUTO,INPUT_PULLUP);

  pinMode(BUZZER,OUTPUT);

  ledcAttach(PWMA,PWM_FREQ,PWM_RES);

  stopMotor();

  Serial.println("");
  Serial.println("========================");
  Serial.println("Sistema iniciado");
  Serial.println("========================");

  Serial.print("Tiempo guardado: ");
  Serial.print(tiempoMax/1000.0);
  Serial.println(" s");
}


//=================================================

void loop() {

  detectarProgramacion();

  //============== MODO PROGRAMACION ==============

  if(modoProgramacion){

      if(digitalRead(BTN_UP)==LOW){

          if(ultimoEstado!="ARRIBA"){

              Serial.println("");
              Serial.println(">>> AJUSTANDO ARRIBA");

              ultimoEstado="ARRIBA";
          }

          if(inicioTiempo==0)
              inicioTiempo=millis();

          openMotor();

          mostrarTiempo();
      }

      else if(digitalRead(BTN_DOWN)==LOW){

          if(ultimoEstado!="ABAJO"){

              Serial.println("");
              Serial.println(">>> AJUSTANDO ABAJO");

              ultimoEstado="ABAJO";
          }

          if(inicioTiempo==0)
              inicioTiempo=millis();

          closeMotor();

          mostrarTiempo();
      }

      else{

          stopMotor();

          guardarTiempoParcial();

          ultimoEstado="";
      }


      // guardar configuración
      if(digitalRead(BTN_STOP)==LOW){

          stopMotor();

          guardarTiempoParcial();

          tiempoMax=
          tiempoAcumulado;

          prefs.putULong(
          "tiempo",
          tiempoMax);

          Serial.println("");
          Serial.println(
          "CONFIGURACION GUARDADA");

          Serial.print(
          "Tiempo: ");

          Serial.print(
          tiempoMax/1000.0);

          Serial.println(
          " segundos");

          beep(2);

          tiempoAcumulado=0;
          inicioTiempo=0;

          modoProgramacion=false;

          delay(1000);
      }

      return;
  }


  //============== AUTO ==================

  if(digitalRead(BTN_AUTO)==LOW){

      Serial.println("");
      Serial.println(">>> AUTO");

      if(!persianaAbierta){

          Serial.println("Abriendo");

          openMotor();

          delay(tiempoMax);

          stopMotor();

          persianaAbierta=true;

          beep(1);
      }

      else{

          Serial.println("Cerrando");

          closeMotor();

          delay(tiempoMax);

          stopMotor();

          persianaAbierta=false;

          beep(1);
      }

      delay(1000);
  }


  //============== MANUAL =================

  if(digitalRead(BTN_UP)==LOW){

      if(ultimoEstado!="ABRIENDO"){

          Serial.println("");
          Serial.println(">>> ABRIENDO");

          ultimoEstado="ABRIENDO";
      }

      openMotor();
  }

  else if(digitalRead(BTN_DOWN)==LOW){

      if(ultimoEstado!="CERRANDO"){

          Serial.println("");
          Serial.println(">>> CERRANDO");

          ultimoEstado="CERRANDO";
      }

      closeMotor();
  }

  else if(digitalRead(BTN_STOP)==LOW){

      stopMotor();

      if(ultimoEstado!="STOP"){

          Serial.println("");
          Serial.println(">>> DETENIDO");

          ultimoEstado="STOP";
      }
  }

  else{

      stopMotor();

      ultimoEstado="";
  }

  delay(100);
}


//=================================================

void detectarProgramacion(){

    static unsigned long inicio=0;

    if(digitalRead(BTN_STOP)==LOW){

        if(inicio==0)
            inicio=millis();

        if(
        (millis()-inicio)>3000 &&
        !modoProgramacion){

            modoProgramacion=true;

            tiempoAcumulado=0;
            inicioTiempo=0;

            Serial.println("");
            Serial.println(
            ">>> MODO PROGRAMACION");

            beep(1);

            inicio=0;

            delay(1000);
        }
    }

    else{

      inicio=0;
    }
}


//=================================================

void mostrarTiempo(){

  static unsigned long ultimo=9999;

  unsigned long actual=
  tiempoAcumulado;

  if(inicioTiempo!=0){

      actual +=
      millis()-inicioTiempo;
  }

  unsigned long segundos=
  actual/1000;

  if(segundos!=ultimo){

      ultimo=segundos;

      Serial.print(
      "Tiempo: ");

      Serial.print(segundos);

      Serial.println(
      " segundos");
  }
}


//=================================================

void guardarTiempoParcial(){

   if(inicioTiempo!=0){

      tiempoAcumulado+=
      millis()-inicioTiempo;

      inicioTiempo=0;
   }
}


//=================================================

void openMotor(){

  digitalWrite(AIN1,HIGH);
  digitalWrite(AIN2,LOW);

  ledcWrite(PWMA,MOTOR_SPEED);
}


//=================================================

void closeMotor(){

  digitalWrite(AIN1,LOW);
  digitalWrite(AIN2,HIGH);

  ledcWrite(PWMA,MOTOR_SPEED);
}


//=================================================

void stopMotor(){

  digitalWrite(AIN1,LOW);
  digitalWrite(AIN2,LOW);

  ledcWrite(PWMA,0);
}


//=================================================

void beep(int veces){

   for(int i=0;i<veces;i++){

      digitalWrite(
      BUZZER,HIGH);

      delay(150);

      digitalWrite(
      BUZZER,LOW);

      delay(150);
   }
}
